# Fritzing sketch JARL_Circuit (saved by Fritzing 0.9.3b)
breadboards: 1

parts:
  Part1 = Adafruit nRF8001 Breakout [part_number="Adafruit #1697"]
  DRV_1 = DRV 8825 Stepper Motor Carrier, High Current [part_number="DRV 8825"]
  DRV_2 = DRV 8825 Stepper Motor Carrier, High Current [part_number="DRV 8825"]
  DRV_3 = DRV 8825 Stepper Motor Carrier, High Current [part_number="DRV 8825"]
  C1 = Ceramic Capacitor [capacitance=0.1mF package="0603 [SMD, multilayer]"]
  C2 = Ceramic Capacitor [capacitance=0.1mF package="0603 [SMD, multilayer]"]
  C3 = Ceramic Capacitor [capacitance=0.1mF package="0603 [SMD, multilayer]"]
  M2 = Stepper Motor - Bipolar
  M3 = Stepper Motor - Bipolar
  M4 = Stepper Motor - Bipolar
  Part2 = Arduino Uno (Rev3) - ICSP
  VCC1 = Battery block 9V
  IC1 = Voltage Regulator [package=to-220-alt]
  C4 = Ceramic Capacitor [capacitance=1µF package="0603 [SMD, multilayer]"]
  C5 = Ceramic Capacitor [capacitance=1µF package="0603 [SMD, multilayer]"]

nets:
  N1: Part1.SCK, Part2.D13/SCK
  N2: Part1.MISO, Part2.D12/MISO
  N3: Part1.MOSI, Part2.D11_PWM/MOSI
  N4: Part1.REQN, Part2.D10_PWM/SS
  N5: Part1.RDYN, Part2.D2
  N6: Part1.RESET, Part2.D9_PWM
  GND: Part1.GND, DRV_1.GROUND_ST/_MT, DRV_1.GROUND_LOG, DRV_2.GROUND_ST/_MT, DRV_2.GROUND_LOG, DRV_3.GROUND_ST/_MT, DRV_3.GROUND_LOG, C1.1, C2.1, C3.1, Part2.GND, VCC1.-, IC1.IN, C4.0, C5.1
  VIN: Part1.VIN, DRV_1.MS1, DRV_1.MS2, DRV_1.MS3, DRV_1.RESET, DRV_1.SLEEP, DRV_2.MS1, DRV_2.MS2, DRV_2.MS3, DRV_2.RESET, DRV_2.SLEEP, DRV_3.MS1, DRV_3.MS2, DRV_3.MS3, DRV_3.RESET, DRV_3.SLEEP, Part2.5V, IC1.OUT, C5.0
  N7: DRV_1.STEP, Part2.D4
  N8: DRV_1.DIRECTION, Part2.D3_PWM
  N9: DRV_1.VOLTAGE_ST/_MT, DRV_2.VOLTAGE_ST/_MT, DRV_3.VOLTAGE_ST/_MT, C1.0, C2.0, C3.0, VCC1.+, IC1.GND, C4.1
  N10: DRV_1.OUT_2B, M2.A
  N11: DRV_1.OUT_2A, M2.C
  N12: DRV_1.OUT_1A, M2.B
  N13: DRV_1.OUT_1B, M2.D
  N14: DRV_2.STEP, Part2.D6_PWM
  N15: DRV_2.DIRECTION, Part2.D5_PWM
  N16: DRV_2.OUT_2B, M3.A
  N17: DRV_2.OUT_2A, M3.C
  N18: DRV_2.OUT_1A, M3.B
  N19: DRV_2.OUT_1B, M3.D
  N20: DRV_3.STEP, Part2.D8
  N21: DRV_3.DIRECTION, Part2.D7
  N22: DRV_3.OUT_2B, M4.A
  N23: DRV_3.OUT_2A, M4.C
  N24: DRV_3.OUT_1A, M4.B
  N25: DRV_3.OUT_1B, M4.D

custom parts:
  Adafruit nRF8001 Breakout: Our Adafruit Bluefruit LE (Bluetooth Smart, Bluetooth Low Energy, Bluetooth 4.0) nRF8001 Breakout allows you to establish an easy to use wireless link between your Arduino and any compatible iOS or Android (4.3+) device. It works by simulating a UART device beneath the surface, sending ASCII data back and forth between the devices, letting you decide what data to send and what to do with it on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
